# Fritzing sketch schematics (saved by Fritzing 0.9.4)
circuit board: 8.46667cm x 5.64444cm
breadboards: 1

parts:
  980 = Resistor [tolerance=±5% resistance=980 package=THT]
  510 = Resistor [tolerance=±5% resistance=510 package=THT]
  680 = Resistor [tolerance=±5% resistance=680 package=THT]
  330 = Resistor [tolerance=±5% resistance=330 package=THT]
  220 = Resistor [tolerance=±5% resistance=220 package=THT]
  100 = Resistor [tolerance=±5% resistance=100 package=THT]
  S1 = Pushbutton [package="[THT]"]
  S2 = Pushbutton [package="[THT]"]
  S4 = Pushbutton [package="[THT]"]
  S5 = Pushbutton [package="[THT]"]
  C2 = Ceramic Capacitor [capacitance=0.47mF package="1206 [SMD, multilayer]"]
  S6 = Pushbutton [package="[THT]"]
  Pot = POT [package=pot_alpha_rv16af-20]
  S3 = Pushbutton [package="[THT]"]
  J1 = female pin header, 4 pins [form="♀ (female)"]
  Part1 = Arduino Uno (Rev3) - ICSP
  330_video = Resistor [tolerance=±5% resistance=330 package=THT]
  470_video = Resistor [tolerance=±5% resistance=470 package=THT]
  Composite_Out = female pin header, 2 pins [form="♀ (female)"]

nets:
  N1: 980.Pin_0, C2.1, Pot.A, J1.pin4, Part1.GND, Composite_Out.pin1
  N2: 980.Pin_1, S1.Pin_3, S1.Pin_4, S2.Pin_3, S2.Pin_4, S4.Pin_3, S4.Pin_4, S5.Pin_3, S5.Pin_4, C2.0, S6.Pin_3, S6.Pin_4, S3.Pin_3, S3.Pin_4, J1.pin3, Part1.A5/SCL
  N3: 510.Pin_0, 680.Pin_0, 330.Pin_0, 220.Pin_0, 100.Pin_0, S6.Pin_1, S6.Pin_2, Pot.E, J1.pin1, Part1.5V
  N4: 510.Pin_1, S2.Pin_1, S2.Pin_2
  N5: 680.Pin_1, S1.Pin_1, S1.Pin_2
  N6: 330.Pin_1, S3.Pin_1, S3.Pin_2
  N7: 220.Pin_1, S4.Pin_1, S4.Pin_2
  N8: 100.Pin_1, S5.Pin_1, S5.Pin_2
  N9: Pot.S, J1.pin2, Part1.A0
  N10: Part1.D9_PWM, 470_video.Pin_1
  N11: Part1.D7, 330_video.Pin_1
  N12: 330_video.Pin_0, 470_video.Pin_0, Composite_Out.pin2
